# Fritzing sketch Raspberry and buttons (saved by Fritzing 0.9.3b)

parts:
  Raspberry_Pi_1 = Raspberry Pi 3 [part_number=RPI-3-V1.2]
  S1 = Round Pushbutton
  S2 = Round Pushbutton

nets:
  N1: Raspberry_Pi_1.GPIO26, S2.leg0
  N2: Raspberry_Pi_1.GPIO16, S1.leg0
  N3: Raspberry_Pi_1.GND, S1.leg1, S2.leg1
